# Fritzing sketch wires (saved by Fritzing 0.9.3b)

parts:
  Part2 = Arduino Nano (Rev3.0)
  NRF24L3 = NRF24L01

nets:
  N1: Part2.D9, NRF24L3.CE
  N2: Part2.D10, NRF24L3.CSN
  N3: Part2.D11/MOSI, NRF24L3.MOSI
  N4: Part2.D12/MISO, NRF24L3.MISO
  GND: Part2.GND, NRF24L3.GND
  3V3: Part2.3V3, NRF24L3.VCC
  N5: Part2.D13/SCK, NRF24L3.SCK

custom parts:
  NRF24L01: NRF24L01 module
